// Logisim project ex2.circ as structural Verilog
module meia_soma (
  input  X0,
  input  y0,
  output out_3,
  output out_4
);

  and and_1 (out_4, y0, X0);
  xor xor_1 (out_3, X0, y0);
endmodule

module soma_comp (
  input  in_1,
  input  in_2,
  input  in_3,
  output out_4,
  output out_5
);

  wire meia_soma_1_out_3, meia_soma_1_out_4, meia_soma_2_out_4;

  meia_soma meia_soma_1 (.X0(in_2), .y0(in_3), .out_4(meia_soma_1_out_4), .out_3(meia_soma_1_out_3));
  meia_soma meia_soma_2 (.X0(in_1), .y0(meia_soma_1_out_3), .out_4(meia_soma_2_out_4), .out_3(out_4));
  or or_1 (out_5, meia_soma_1_out_4, meia_soma_2_out_4);
endmodule

module som_4_bits (
  input  x0,
  input  y0,
  input  x1,
  input  y1,
  input  x2,
  input  y2,
  input  x3,
  input  x4,
  output z0,
  output z1,
  output z2,
  output z3,
  output COUT
);

  wire meia_soma_1_out_4, soma_comp_1_out_5, soma_comp_2_out_5;

  meia_soma meia_soma_1 (.X0(x0), .y0(y0), .out_4(meia_soma_1_out_4), .out_3(z0));
  soma_comp soma_comp_1 (.in_2(x1), .in_3(y1), .in_1(meia_soma_1_out_4), .out_5(soma_comp_1_out_5), .out_4(z1));
  soma_comp soma_comp_2 (.in_2(x2), .in_3(y2), .in_1(soma_comp_1_out_5), .out_5(soma_comp_2_out_5), .out_4(z2));
  soma_comp soma_comp_3 (.in_2(x3), .in_3(x4), .in_1(soma_comp_2_out_5), .out_5(COUT), .out_4(z3));
endmodule

module ula_ex2 (
  input  [3:0] in_1,
  input  [3:0] in_2,
  input  [3:0] in_3,
  output [3:0] out_4
);

  wire multiplexer_1_p4;
  wire [3:0] not_1_out, or_1_out;

  assign not_1_out = ~in_1;  // NOT_Gate not_1, 4 bits wide
  assign or_1_out = in_1 | in_2;  // OR_Gate or_1, 4 bits wide
  // Multiplexer #(.select(4), .width(4), .enable("false")) multiplexer_1: pin names not known; wires that end beside it: not_1_out, or_1_out, 4'b0000, multiplexer_1_p4, multiplexer_1_p4, in_3, out_4
endmodule
