// Logisim project ex2pt2.circ as structural Verilog
module meia_soma (
  input  X0,
  input  y0,
  output out_3,
  output out_4
);

  and and_1 (out_4, y0, X0);
  xor xor_1 (out_3, X0, y0);
endmodule

module soma_comp (
  input  in_1,
  input  in_2,
  input  in_3,
  output out_4,
  output out_5
);

  wire meia_soma_1_out_3, meia_soma_1_out_4, meia_soma_2_out_4;

  meia_soma meia_soma_1 (.X0(in_2), .y0(in_3), .out_4(meia_soma_1_out_4), .out_3(meia_soma_1_out_3));
  meia_soma meia_soma_2 (.X0(in_1), .y0(meia_soma_1_out_3), .out_4(meia_soma_2_out_4), .out_3(out_4));
  or or_1 (out_5, meia_soma_1_out_4, meia_soma_2_out_4);
endmodule

module som_4_bits (
  input  x0,
  input  y0,
  input  x1,
  input  y1,
  input  x2,
  input  y2,
  input  x3,
  input  x4,
  output z0,
  output z1,
  output z2,
  output z3,
  output COUT
);

  wire meia_soma_1_out_4, soma_comp_1_out_5, soma_comp_2_out_5;

  meia_soma meia_soma_1 (.X0(x0), .y0(y0), .out_4(meia_soma_1_out_4), .out_3(z0));
  soma_comp soma_comp_1 (.in_2(x1), .in_3(y1), .in_1(meia_soma_1_out_4), .out_5(soma_comp_1_out_5), .out_4(z1));
  soma_comp soma_comp_2 (.in_2(x2), .in_3(y2), .in_1(soma_comp_1_out_5), .out_5(soma_comp_2_out_5), .out_4(z2));
  soma_comp soma_comp_3 (.in_2(x3), .in_3(x4), .in_1(soma_comp_2_out_5), .out_5(COUT), .out_4(z3));
endmodule

module ula_ex2 (
  input  [3:0] A,
  input  [3:0] B,
  input  [3:0] in_3,
  output [3:0] out_4
);

  wire [3:0] and_1_out, and_2_out, and_3_out, nor_1_out, not_1_out, not_2_out, not_3_out, not_4_out,
       not_5_out, or_1_out, or_2_out, or_3_out, or_4_out, or_5_out, xnor_1_out;

  assign not_1_out = ~B;  // NOT_Gate not_1, 4 bits wide
  assign or_1_out = not_1_out | A;  // OR_Gate or_1, 4 bits wide
  assign not_2_out = ~A;  // NOT_Gate not_2, 4 bits wide
  assign not_3_out = ~B;  // NOT_Gate not_3, 4 bits wide
  assign not_4_out = ~A;  // NOT_Gate not_4, 4 bits wide
  assign or_2_out = A | B;  // OR_Gate or_2, 4 bits wide
  assign or_3_out = not_4_out | not_1_out;  // OR_Gate or_3, 4 bits wide
  assign and_1_out = A & B;  // AND_Gate and_1, 4 bits wide
  assign or_4_out = A | A;  // OR_Gate or_4, 4 bits wide
  assign xnor_1_out = ~(B ^ A);  // XNOR_Gate xnor_1, 4 bits wide
  assign nor_1_out = ~(not_2_out | not_3_out);  // NOR_Gate nor_1, 4 bits wide
  assign or_5_out = not_2_out | B;  // OR_Gate or_5, 4 bits wide
  assign and_2_out = not_3_out & A;  // AND_Gate and_2, 4 bits wide
  assign and_3_out = not_4_out & B;  // AND_Gate and_3, 4 bits wide
  Multiplexer #(.select(4), .width(4), .enable("false")) multiplexer_1 (
    .in0(not_4_out), .in1(or_2_out), .in2(and_3_out), .in3(4'b0000), .in4(or_3_out), .in5(A),
    .in6(xnor_1_out), .in7(and_2_out), .in8(or_5_out), .in9(not_5_out), .in10(B), .in11(and_1_out),
    .in12(4'b0001), .in13(or_1_out), .in14(or_4_out), .in15(A), .out(out_4), .sel(in_3));
  assign not_5_out = ~nor_1_out;  // NOT_Gate not_5, 4 bits wide
endmodule
